// Logisim project 1Parc_EMANOVA_ULTIMATE_KOLEKCIJA.circ as structural Verilog
module EXCESS_3_BCD_To_Display_Zadatak1 (
  input  x0,
  input  x1,
  input  x2,
  input  x3
);

  wire A, and_1_out, and_2_out, B, C, D, E, F, G, multiplexer_1_out, multiplexer_2_out, multiplexer_3_out,
       multiplexer_4_out, multiplexer_8_out, multiplexer_9_out, nand_1_out, nand_2_out, nor_1_out, nor_2_out,
       nor_3_out, nor_4_out, nor_5_out, nor_6_out, nor_7_out, not_1_out, not_2_out;
  wire [0:0] multiplexer_6_out;

  Multiplexer multiplexer_1 (.in0(1'b1), .in1(1'b0), .out(multiplexer_1_out), .sel(x1));
  Multiplexer multiplexer_2 (.in0(1'b1), .in1(1'b0), .out(multiplexer_2_out), .sel(x2));
  not not_1 (not_1_out, x3);
  nor nor_1 (nor_1_out, x0, x0);
  nor nor_2 (nor_2_out, x2, x2);
  nor nor_3 (nor_3_out, x3, x3);
  nor nor_4 (nor_4_out, x1, x1);
  nand nand_1 (nand_1_out, x1, x2);
  not not_2 (not_2_out, x2);
  Multiplexer multiplexer_3 (.in0(multiplexer_1_out), .in1(1'b1), .out(multiplexer_3_out), .sel(x0));
  Multiplexer multiplexer_4 (.in0(x2), .in1(multiplexer_2_out), .out(multiplexer_4_out), .sel(x3));
  Multiplexer #(.select(3)) multiplexer_5 (
    .in0(1'b1), .in1(1'b1), .in2(1'b1), .in3(1'b1), .in4(1'b0), .in5(1'b1), .in6(1'b1), .in7(1'b1), .out(B),
    .sel({x0, x1, x2}));
  nand nand_2 (nand_2_out, nand_1_out, x3);
  nand nand_3 (E, nand_2_out, nand_2_out);
  and and_1 (and_1_out, x2, x3);
  or or_1 (F, and_1_out, and_2_out);
  and and_2 (and_2_out, x0, not_2_out);
  Multiplexer #(.select(2)) multiplexer_6 (
    .in0(1'b1), .in1(1'b0), .out(multiplexer_6_out[0]), .sel({1'b0, x2}));  // open: in2, in3
  Multiplexer multiplexer_7 (.in0(multiplexer_3_out), .in1(1'b1), .out(A), .sel(multiplexer_4_out));
  or or_2 (C, x0, x2, not_1_out);
  nor nor_5 (nor_5_out, nor_1_out, nor_2_out, x3);
  nor nor_6 (nor_6_out, nor_3_out, nor_4_out, nor_2_out);
  nor nor_7 (nor_7_out, x3, x2, x0);
  Multiplexer #(.select(2)) multiplexer_8 (
    .in0(x3), .in1(1'b1), .out(multiplexer_8_out), .sel({1'b0, multiplexer_6_out[0]}));  // open: in2, in3
  Multiplexer #(.select(2)) multiplexer_9 (
    .in0(x2), .in1(1'b1), .out(multiplexer_9_out), .sel({1'b0, x3}));  // open: in2, in3
  nor nor_8 (D, nor_5_out, nor_6_out, nor_7_out);
  Multiplexer #(.select(2)) multiplexer_10 (
    .in0(1'b0), .in1(multiplexer_9_out), .in2(multiplexer_8_out), .in3(1'b1), .out(G), .sel({x0, x1}));
  _7_Segment_Display u_7_segment_display_1 (.g(G), .f(F), .a(A), .b(B), .e(E), .d(D), .c(C), .dp(1'b1));
endmodule

module HALF_ADD_1bit (
  input  x,
  input  y,
  output S,
  output C
);

  xor xor_1 (S, y, x);
  and and_1 (C, y, x);
endmodule

module FULL_ADD_1bit (
  input  x,
  input  y,
  input  z,
  output S,
  output C
);

  wire and_1_out, and_2_out, xor_1_out;

  xor xor_1 (xor_1_out, y, x);
  and and_1 (and_1_out, x, y);
  xor xor_2 (S, z, xor_1_out);
  and and_2 (and_2_out, z, xor_1_out);
  or or_1 (C, and_2_out, and_1_out);
endmodule

module ADD_1bit (
  input  A,
  input  B,
  input  Cin,
  output R,
  output Cout
);

  wire and_1_out, not_1_out, or_1_out, xor_1_out;

  xor xor_1 (xor_1_out, A, B);
  and and_1 (and_1_out, A, B);
  or or_1 (or_1_out, B, A);
  not not_1 (not_1_out, xor_1_out);
  Multiplexer multiplexer_1 (.in0(and_1_out), .in1(or_1_out), .out(Cout), .sel(Cin));
  Multiplexer multiplexer_2 (.in0(xor_1_out), .in1(not_1_out), .out(R), .sel(Cin));
endmodule

module ADD_4bit (
  input  [3:0] A,
  input  [3:0] B,
  output [3:0] out_3,
  output C
);

  wire add_1bit_1_cout, add_1bit_2_cout, add_1bit_3_cout;

  ADD_1bit add_1bit_1 (.A(A[0]), .B(B[0]), .R(out_3[0]), .Cout(add_1bit_1_cout));  // open: Cin
  ADD_1bit add_1bit_2 (.A(A[1]), .B(B[1]), .Cin(add_1bit_1_cout), .R(out_3[1]), .Cout(add_1bit_2_cout));
  ADD_1bit add_1bit_3 (.A(A[2]), .B(B[2]), .Cin(add_1bit_2_cout), .R(out_3[2]), .Cout(add_1bit_3_cout));
  ADD_1bit add_1bit_4 (.A(A[3]), .B(B[3]), .Cin(add_1bit_3_cout), .R(out_3[3]), .Cout(C));
endmodule

module HALF_SUBSTRACT_1bit (
  input  x,
  input  y,
  output R,
  output C
);

  wire not_1_out;

  xor xor_1 (R, x, y);
  not not_1 (not_1_out, x);
  and and_1 (C, not_1_out, y);

  // Notes on the sheet:
  //   c je bit posudbe
endmodule

module FULL_SUBSTRACT_1bit (
  input  cIn,
  input  A,
  input  B,
  output R,
  output cOut
);

  wire and_1_out, and_2_out, and_3_out, and_4_out, and_5_out, and_6_out, and_7_out, not_1_out, not_2_out,
       not_3_out;

  not not_1 (not_1_out, cIn);
  not not_2 (not_2_out, A);
  not not_3 (not_3_out, B);
  and and_1 (and_1_out, not_1_out, not_2_out, B);
  and and_2 (and_2_out, not_1_out, A, not_3_out);
  and and_3 (and_3_out, cIn, not_2_out, not_3_out);
  and and_4 (and_4_out, cIn, A, B);
  and and_5 (and_5_out, not_2_out, B);
  and and_6 (and_6_out, cIn, not_2_out);
  and and_7 (and_7_out, cIn, B);
  or or_1 (R, and_1_out, and_2_out, and_3_out, and_4_out);
  or or_2 (cOut, and_5_out, and_6_out, and_7_out);
endmodule

module FULL_SUBSTRACT_1bit_NOR (
  input  cin,
  input  a,
  input  b,
  output rez,
  output c
);

  wire nor_1_out, nor_2_out, nor_3_out, nor_4_out, nor_5_out, nor_6_out, nor_7_out, nor_8_out, nor_9_out,
       nor_10_out;

  nor nor_1 (nor_1_out, cin, cin);
  nor nor_2 (nor_2_out, a, a);
  nor nor_3 (nor_3_out, b, b);
  nor nor_4 (nor_4_out, cin, nor_2_out, nor_3_out);
  nor nor_5 (nor_5_out, nor_2_out, b, nor_1_out);
  nor nor_6 (nor_6_out, a, a, nor_1_out);
  nor nor_7 (nor_7_out, a, cin, b);
  nor nor_8 (nor_8_out, cin, nor_2_out);
  nor nor_9 (nor_9_out, nor_2_out, b);
  nor nor_10 (nor_10_out, cin, b);
  nor nor_11 (rez, nor_4_out, nor_5_out, nor_6_out, nor_7_out);
  nor nor_12 (c, nor_8_out, nor_9_out, nor_10_out);
endmodule

module SUBSTRACT_4bit (
  input  [3:0] A,
  input  [3:0] B,
  output [3:0] out_3,
  output C
);

  wire add_1bit_1_r, add_1bit_2_r, add_1bit_3_r, add_1bit_4_cout, add_1bit_4_r, add_1bit_8_cout, c1, c2, c3,
       p1, p2, p3;
  wire [3:0] not_1_out;

  assign not_1_out = ~B;  // NOT_Gate not_1, 4 bits wide
  ADD_1bit add_1bit_1 (.A(not_1_out[0]), .B(1'b1), .R(add_1bit_1_r), .Cout(c1));  // open: Cin
  ADD_1bit add_1bit_2 (.A(not_1_out[1]), .B(c1), .R(add_1bit_2_r), .Cout(c2));  // open: Cin
  ADD_1bit add_1bit_3 (.A(not_1_out[2]), .B(c2), .R(add_1bit_3_r), .Cout(c3));  // open: Cin
  ADD_1bit add_1bit_4 (.A(not_1_out[3]), .B(c3), .R(add_1bit_4_r), .Cout(add_1bit_4_cout));  // open: Cin
  ADD_1bit add_1bit_5 (.A(A[0]), .B(add_1bit_1_r), .R(out_3[0]), .Cout(p1));  // open: Cin
  ADD_1bit add_1bit_6 (.A(A[1]), .B(add_1bit_2_r), .Cin(p1), .R(out_3[1]), .Cout(p2));
  ADD_1bit add_1bit_7 (.A(A[2]), .B(add_1bit_3_r), .Cin(p2), .R(out_3[2]), .Cout(p3));
  ADD_1bit add_1bit_8 (.A(A[3]), .B(add_1bit_4_r), .Cin(p3), .R(out_3[3]), .Cout(add_1bit_8_cout));
  ADD_1bit add_1bit_9 (.A(add_1bit_8_cout), .B(add_1bit_4_cout), .R(C));  // open: Cin, Cout
endmodule

module SUBSTRACT_8bit (
  input  [7:0] in_1,
  input  [7:0] in_2,
  output [7:0] out_3,
  output out_4
);

  wire substract_4bit_2_p4, substract_4bit_3_c;
  wire [0:0] substract_4bit_1_c;
  wire [3:0] add_4bit_1_out_3, substract_4bit_2_p3;

  SUBSTRACT_4bit substract_4bit_1 (.A(in_1[3:0]), .B(in_2[3:0]), .out_3(out_3[3:0]), .C(substract_4bit_1_c[0]));
  // SUBSTRACT_4bit substract_4bit_2: pin names not known; wires that end beside it: in_1[7:4], in_2[7:4], substract_4bit_2_p3, substract_4bit_2_p4
  ADD_4bit add_4bit_1 (
    .A({3'b000, substract_4bit_1_c[0]}), .B(substract_4bit_2_p3), .out_3(add_4bit_1_out_3));  // open: C
  SUBSTRACT_4bit substract_4bit_3 (.A(add_4bit_1_out_3), .B(4'b0001), .out_3(out_3[7:4]), .C(substract_4bit_3_c));
  ADD_1bit add_1bit_1 (.A(substract_4bit_3_c), .B(substract_4bit_2_p4), .R(out_4));  // open: Cin, Cout
endmodule

module NOT_AB_1bit (
  input  A,
  input  B,
  output notAB
);

  wire nor_1_out, nor_2_out, nor_3_out;

  nor nor_1 (nor_1_out, A, A);
  nor nor_2 (nor_2_out, B, B);
  nor nor_3 (nor_3_out, nor_1_out, nor_2_out);
  nor nor_4 (notAB, nor_3_out, nor_3_out);
endmodule

module A_OR_B_1bit (
  input  A,
  input  B,
  output A_OR_B
);

  wire nand_1_out, nand_2_out;

  nand nand_1 (nand_1_out, 1'b1, A);
  nand nand_2 (nand_2_out, 1'b1, B);
  nand nand_3 (A_OR_B, nand_1_out, nand_2_out);
endmodule

module ALU_1bit (
  input  Cin,
  input  A,
  input  B,
  input  [1:0] S,
  output C,
  output Rez
);

  wire a_or_b_1bit_1_a_or_b, full_substract_1bit_1_r, not_1_out, not_ab_1bit_1_notab;

  not not_1 (not_1_out, B);
  FULL_SUBSTRACT_1bit full_substract_1bit_1 (.cIn(Cin), .A(A), .B(B), .R(full_substract_1bit_1_r), .cOut(C));
  NOT_AB_1bit not_ab_1bit_1 (.A(A), .B(B), .notAB(not_ab_1bit_1_notab));
  A_OR_B_1bit a_or_b_1bit_1 (.A(A), .B(B), .A_OR_B(a_or_b_1bit_1_a_or_b));
  Multiplexer #(.select(2)) multiplexer_1 (
    .in0(full_substract_1bit_1_r), .in1(not_1_out), .in2(not_ab_1bit_1_notab), .in3(a_or_b_1bit_1_a_or_b),
    .out(Rez), .sel(S));
endmodule

module ALU_8bit_Zadatak2 (
  input  [1:0] S,
  input  [7:0] A,
  input  [7:0] B,
  output [7:0] R
);

  wire c1, c2, c3, c4, c5, c6, c7;

  ALU_1bit alu_1bit_1 (.Cin(1'b0), .A(A[0]), .B(B[0]), .S(S), .C(c1), .Rez(R[0]));
  ALU_1bit alu_1bit_2 (.Cin(c1), .A(A[1]), .B(B[1]), .S(S), .C(c2), .Rez(R[1]));
  ALU_1bit alu_1bit_3 (.Cin(c2), .A(A[2]), .B(B[2]), .S(S), .C(c3), .Rez(R[2]));
  ALU_1bit alu_1bit_4 (.Cin(c3), .A(A[3]), .B(B[3]), .S(S), .C(c4), .Rez(R[3]));
  ALU_1bit alu_1bit_5 (.Cin(c4), .A(A[4]), .B(B[4]), .S(S), .C(c5), .Rez(R[4]));
  ALU_1bit alu_1bit_6 (.Cin(c5), .A(A[5]), .B(B[5]), .S(S), .C(c6), .Rez(R[5]));
  ALU_1bit alu_1bit_7 (.Cin(c6), .A(A[6]), .B(B[6]), .S(S), .C(c7), .Rez(R[6]));
  ALU_1bit alu_1bit_8 (.Cin(c7), .A(A[7]), .B(B[7]), .S(S), .Rez(R[7]));  // open: C

  // Other names for the same wires on the sheet: A1 = A[0]; A2 = A[1]; A3 = A[2]; A4 = A[3]; A5 = A[4]; A6 = A[5];
  //   A7 = A[6]; A8 = A[7]; B1 = B[0]; B2 = B[1]; B3 = B[2]; B4 = B[3]; B5 = B[4]; B6 = B[5]; B7 = B[6]; B8 = B[7]
endmodule

module MUX8u1 (
  input  U0,
  input  U1,
  input  U2,
  input  U3,
  input  U4,
  input  U5,
  input  U6,
  input  U7,
  input  [2:0] S2S1S0,
  output out_10
);

  wire nand_4_out, nand_5_out, nand_6_out, nand_7_out, nand_9_out, nand_10_out, nand_11_out, nand_12_out,
       notS0, notS1, notS2;

  nand nand_1 (notS0, S2S1S0[0], S2S1S0[0]);
  nand nand_2 (notS1, S2S1S0[1], S2S1S0[1]);
  nand nand_3 (notS2, S2S1S0[2], S2S1S0[2]);
  nand nand_4 (nand_4_out, U0, notS2, notS1, notS0);
  nand nand_5 (nand_5_out, U1, notS2, notS1, S2S1S0[0]);
  nand nand_6 (nand_6_out, U2, notS2, S2S1S0[1], notS0);
  nand nand_7 (nand_7_out, U3, notS2, S2S1S0[1], S2S1S0[0]);
  nand nand_8 (out_10, nand_7_out, nand_6_out, nand_5_out, nand_4_out, nand_9_out, nand_10_out, nand_11_out, nand_12_out);
  nand nand_9 (nand_9_out, U4, S2S1S0[2], notS1, notS0);
  nand nand_10 (nand_10_out, U5, S2S1S0[2], notS1, S2S1S0[0]);
  nand nand_11 (nand_11_out, U6, S2S1S0[2], S2S1S0[1], notS0);
  nand nand_12 (nand_12_out, U7, S2S1S0[2], S2S1S0[1], S2S1S0[0]);

  // Other names for the same wires on the sheet: A = U7; B = U6; C = U5; D = U4; E = U3; F = U2; G = U1; H = U0;
  //   S0 = S2S1S0[0]; S1 = S2S1S0[1]; S2 = S2S1S0[2]
endmodule

module MUX8x4u8x1 (
  input  [7:0] U0,
  input  [7:0] U1,
  input  [7:0] U2,
  input  [7:0] U3,
  input  [1:0] S1S0,
  output [7:0] out_6
);

  wire [7:0] nand_3_out, nand_4_out, nand_5_out, nand_6_out, notS08, notS18, S08, S18;

  assign S08 = {{7{S1S0[0]}}, S1S0[0]};  // Bit_Extender bit_extender_1
  assign S18 = {{7{S1S0[1]}}, S1S0[1]};  // Bit_Extender bit_extender_2
  assign notS08 = ~(S08 & S08);  // NAND_Gate nand_1, 8 bits wide
  assign notS18 = ~(S18 & S18);  // NAND_Gate nand_2, 8 bits wide
  assign nand_3_out = ~(U3 & S08 & S18);  // NAND_Gate nand_3, 8 bits wide
  assign nand_4_out = ~(U2 & notS08 & S18);  // NAND_Gate nand_4, 8 bits wide
  assign nand_5_out = ~(U1 & S08 & notS18);  // NAND_Gate nand_5, 8 bits wide
  assign nand_6_out = ~(U0 & notS08 & notS18);  // NAND_Gate nand_6, 8 bits wide
  assign out_6 = ~(nand_4_out & nand_3_out & nand_5_out & nand_6_out);  // NAND_Gate nand_7, 8 bits wide

  // Other names for the same wires on the sheet: A[7:0] = U3; B[7:0] = U2; C[7:0] = U1; D[7:0] = U0
endmodule

module BS_RightMov (
  input  [7:0] A,
  input  [2:0] C,
  output [7:0] D
);

  MUX8u1 mux8u1_1 (
    .U0(A[7]), .U1(1'b0), .U2(1'b0), .U3(1'b0), .U4(1'b0), .U5(1'b0), .U6(1'b0), .U7(1'b0), .S2S1S0(C),
    .out_10(D[7]));
  MUX8u1 mux8u1_2 (
    .U0(A[6]), .U1(A[7]), .U2(1'b0), .U3(1'b0), .U4(1'b0), .U5(1'b0), .U6(1'b0), .U7(1'b0), .S2S1S0(C),
    .out_10(D[6]));
  MUX8u1 mux8u1_3 (
    .U0(A[5]), .U1(A[6]), .U2(A[7]), .U3(1'b0), .U4(1'b0), .U5(1'b0), .U6(1'b0), .U7(1'b0), .S2S1S0(C),
    .out_10(D[5]));
  MUX8u1 mux8u1_4 (
    .U0(A[4]), .U1(A[5]), .U2(A[6]), .U3(A[7]), .U4(1'b0), .U5(1'b0), .U6(1'b0), .U7(1'b0), .S2S1S0(C),
    .out_10(D[4]));
  MUX8u1 mux8u1_5 (
    .U0(A[3]), .U1(A[4]), .U2(A[5]), .U3(A[6]), .U4(A[7]), .U5(1'b0), .U6(1'b0), .U7(1'b0), .S2S1S0(C),
    .out_10(D[3]));
  MUX8u1 mux8u1_6 (
    .U0(A[2]), .U1(A[3]), .U2(A[4]), .U3(A[5]), .U4(A[6]), .U5(A[7]), .U6(1'b0), .U7(1'b0), .S2S1S0(C),
    .out_10(D[2]));
  MUX8u1 mux8u1_7 (
    .U0(A[1]), .U1(A[2]), .U2(A[3]), .U3(A[4]), .U4(A[5]), .U5(A[6]), .U6(A[7]), .U7(1'b0), .S2S1S0(C),
    .out_10(D[1]));
  MUX8u1 mux8u1_8 (
    .U0(A[0]), .U1(A[1]), .U2(A[2]), .U3(A[3]), .U4(A[4]), .U5(A[5]), .U6(A[6]), .U7(A[7]), .S2S1S0(C),
    .out_10(D[0]));

  // Notes on the sheet:
  //   RightMov for C places
endmodule

module BS_RightRot (
  input  [7:0] A,
  input  [2:0] C,
  output [7:0] D
);

  MUX8u1 mux8u1_1 (
    .U0(A[7]), .U1(A[0]), .U2(A[1]), .U3(A[2]), .U4(A[3]), .U5(A[4]), .U6(A[5]), .U7(A[6]), .S2S1S0(C),
    .out_10(D[7]));
  MUX8u1 mux8u1_2 (
    .U0(A[6]), .U1(A[7]), .U2(A[0]), .U3(A[1]), .U4(A[2]), .U5(A[3]), .U6(A[4]), .U7(A[5]), .S2S1S0(C),
    .out_10(D[6]));
  MUX8u1 mux8u1_3 (
    .U0(A[5]), .U1(A[6]), .U2(A[7]), .U3(A[0]), .U4(A[1]), .U5(A[2]), .U6(A[3]), .U7(A[4]), .S2S1S0(C),
    .out_10(D[5]));
  MUX8u1 mux8u1_4 (
    .U0(A[4]), .U1(A[5]), .U2(A[6]), .U3(A[7]), .U4(A[0]), .U5(A[1]), .U6(A[2]), .U7(A[3]), .S2S1S0(C),
    .out_10(D[4]));
  MUX8u1 mux8u1_5 (
    .U0(A[3]), .U1(A[4]), .U2(A[5]), .U3(A[6]), .U4(A[7]), .U5(A[0]), .U6(A[1]), .U7(A[2]), .S2S1S0(C),
    .out_10(D[3]));
  MUX8u1 mux8u1_6 (
    .U0(A[2]), .U1(A[3]), .U2(A[4]), .U3(A[5]), .U4(A[6]), .U5(A[7]), .U6(A[0]), .U7(A[1]), .S2S1S0(C),
    .out_10(D[2]));
  MUX8u1 mux8u1_7 (
    .U0(A[1]), .U1(A[2]), .U2(A[3]), .U3(A[4]), .U4(A[5]), .U5(A[6]), .U6(A[7]), .U7(A[0]), .S2S1S0(C),
    .out_10(D[1]));
  MUX8u1 mux8u1_8 (
    .U0(A[0]), .U1(A[1]), .U2(A[2]), .U3(A[3]), .U4(A[4]), .U5(A[5]), .U6(A[6]), .U7(A[7]), .S2S1S0(C),
    .out_10(D[0]));

  // Notes on the sheet:
  //   RightRot for C places
endmodule

module BS_LeftMov (
  input  [7:0] A,
  input  [2:0] C,
  output [7:0] D
);

  Multiplexer #(.select(3)) multiplexer_1 (
    .in0(A[6]), .in1(A[5]), .in2(A[4]), .in3(A[3]), .in4(A[2]), .in5(A[1]), .in6(A[0]), .in7(1'b0),
    .out(D[6]), .sel(C));
  MUX8u1 mux8u1_1 (
    .U0(A[7]), .U1(A[6]), .U2(A[5]), .U3(A[4]), .U4(A[3]), .U5(A[2]), .U6(A[1]), .U7(A[0]), .S2S1S0(C),
    .out_10(D[7]));
  MUX8u1 mux8u1_2 (
    .U0(A[5]), .U1(A[4]), .U2(A[3]), .U3(A[2]), .U4(A[1]), .U5(A[0]), .U6(1'b0), .U7(1'b0), .S2S1S0(C),
    .out_10(D[5]));
  MUX8u1 mux8u1_3 (
    .U0(A[4]), .U1(A[3]), .U2(A[2]), .U3(A[1]), .U4(A[0]), .U5(1'b0), .U6(1'b0), .U7(1'b0), .S2S1S0(C),
    .out_10(D[4]));
  MUX8u1 mux8u1_4 (
    .U0(A[3]), .U1(A[2]), .U2(A[1]), .U3(A[0]), .U4(1'b0), .U5(1'b0), .U6(1'b0), .U7(1'b0), .S2S1S0(C),
    .out_10(D[3]));
  MUX8u1 mux8u1_5 (
    .U0(A[2]), .U1(A[1]), .U2(A[0]), .U3(1'b0), .U4(1'b0), .U5(1'b0), .U6(1'b0), .U7(1'b0), .S2S1S0(C),
    .out_10(D[2]));
  MUX8u1 mux8u1_6 (
    .U0(A[1]), .U1(A[0]), .U2(1'b0), .U3(1'b0), .U4(1'b0), .U5(1'b0), .U6(1'b0), .U7(1'b0), .S2S1S0(C),
    .out_10(D[1]));
  MUX8u1 mux8u1_7 (
    .U0(A[0]), .U1(1'b0), .U2(1'b0), .U3(1'b0), .U4(1'b0), .U5(1'b0), .U6(1'b0), .U7(1'b0), .S2S1S0(C),
    .out_10(D[0]));

  // Notes on the sheet:
  //   LeftMov for C places
endmodule

module BS_LeftRot (
  input  [7:0] A,
  input  [2:0] C,
  output [7:0] D
);

  MUX8u1 mux8u1_1 (
    .U0(A[7]), .U1(A[6]), .U2(A[5]), .U3(A[4]), .U4(A[3]), .U5(A[2]), .U6(A[1]), .U7(A[0]), .S2S1S0(C),
    .out_10(D[7]));
  MUX8u1 mux8u1_2 (
    .U0(A[6]), .U1(A[5]), .U2(A[4]), .U3(A[3]), .U4(A[2]), .U5(A[1]), .U6(A[0]), .U7(A[7]), .S2S1S0(C),
    .out_10(D[6]));
  MUX8u1 mux8u1_3 (
    .U0(A[5]), .U1(A[4]), .U2(A[3]), .U3(A[2]), .U4(A[1]), .U5(A[0]), .U6(A[7]), .U7(A[6]), .S2S1S0(C),
    .out_10(D[5]));
  MUX8u1 mux8u1_4 (
    .U0(A[4]), .U1(A[3]), .U2(A[2]), .U3(A[1]), .U4(A[0]), .U5(A[7]), .U6(A[6]), .U7(A[5]), .S2S1S0(C),
    .out_10(D[4]));
  MUX8u1 mux8u1_5 (
    .U0(A[3]), .U1(A[2]), .U2(A[1]), .U3(A[0]), .U4(A[7]), .U5(A[6]), .U6(A[5]), .U7(A[4]), .S2S1S0(C),
    .out_10(D[3]));
  MUX8u1 mux8u1_6 (
    .U0(A[2]), .U1(A[1]), .U2(A[0]), .U3(A[7]), .U4(A[6]), .U5(A[5]), .U6(A[4]), .U7(A[3]), .S2S1S0(C),
    .out_10(D[2]));
  MUX8u1 mux8u1_7 (
    .U0(A[1]), .U1(A[0]), .U2(A[7]), .U3(A[6]), .U4(A[5]), .U5(A[4]), .U6(A[3]), .U7(A[2]), .S2S1S0(C),
    .out_10(D[1]));
  MUX8u1 mux8u1_8 (
    .U0(A[0]), .U1(A[7]), .U2(A[6]), .U3(A[5]), .U4(A[4]), .U5(A[3]), .U6(A[2]), .U7(A[1]), .S2S1S0(C),
    .out_10(D[0]));

  // Notes on the sheet:
  //   LeftRot for C places
endmodule

module BarelShifter_8bit_Zadatak3 (
  input  [7:0] A,
  input  [2:0] C,
  input  M,
  input  S,
  output [7:0] D
);

  wire [7:0] bs_leftmov_1_d, bs_leftrot_1_d, bs_rightmov_1_d, bs_rightrot_1_d;

  // Probe on C
  // Probe on A
  BS_RightRot bs_rightrot_1 (.A(A), .C(C), .D(bs_rightrot_1_d));
  BS_LeftRot bs_leftrot_1 (.A(A), .C(C), .D(bs_leftrot_1_d));
  BS_RightMov bs_rightmov_1 (.A(A), .C(C), .D(bs_rightmov_1_d));
  BS_LeftMov bs_leftmov_1 (.A(A), .C(C), .D(bs_leftmov_1_d));
  MUX8x4u8x1 mux8x4u8x1_1 (
    .U0(bs_rightrot_1_d), .U1(bs_leftrot_1_d), .U2(bs_rightmov_1_d), .U3(bs_leftmov_1_d), .S1S0({M, S}),
    .out_6(D));
  // Probe on D

  // Notes on the sheet:
  //   M = 0 (Rot), M = 1 (Mov), S = 0 (Right), S = 1 (Left)
endmodule

module COMPARE_1bit_NOR (
  input  x,
  input  y,
  input  yVeceIn,
  input  xVeceIn,
  input  jednakiIn,
  output yVeceOut,
  output xVeceOut,
  output jednakiOut
);

  wire nor_6_out, nor_7_out, nor_8_out, nor_9_out, nor_10_out, nor_11_out, nor_12_out, nor_13_out, notCase1,
       notCase2, notCase3, notX, notY;

  nor nor_1 (notX, x, x);
  nor nor_2 (notY, y, y);
  nor nor_3 (notCase1, yVeceIn, yVeceIn);
  nor nor_4 (notCase2, xVeceIn, xVeceIn);
  nor nor_5 (notCase3, jednakiIn, jednakiIn);
  nor nor_6 (nor_6_out, notX, yVeceIn);
  nor nor_7 (nor_7_out, notY, xVeceIn);
  nor nor_8 (nor_8_out, y, notX);
  nor nor_9 (nor_9_out, y, yVeceIn);
  nor nor_10 (nor_10_out, yVeceIn, notCase2);
  nor nor_11 (nor_11_out, x, xVeceIn);
  nor nor_12 (nor_12_out, notCase1, xVeceIn);
  nor nor_13 (nor_13_out, x, notY);
  nor nor_14 (yVeceOut, nor_9_out, nor_10_out, nor_6_out);
  nor nor_15 (xVeceOut, nor_11_out, nor_12_out, nor_7_out);
  nor nor_16 (jednakiOut, notCase3, nor_13_out, nor_8_out);

  // Other names for the same wires on the sheet: Case1 = yVeceIn; Case2 = xVeceIn; Case3 = jednakiIn
endmodule

module COMPARE_1bit_NAND (
  input  A,
  input  B,
  input  in,
  input  in_2,
  input  in_3,
  output out,
  output out_2,
  output out_3
);

  wire nand_1_out, nand_2_out, nand_3_out, nand_4_out, nand_6_out, nand_8_out, nand_9_out, nand_10_out;

  nand nand_1 (nand_1_out, A, B, in_3);
  nand nand_2 (nand_2_out, A, A);
  nand nand_3 (nand_3_out, B, B);
  nand nand_4 (nand_4_out, nand_2_out, B, in_3);
  nand nand_5 (out, nand_4_out, nand_8_out);
  nand nand_6 (nand_6_out, nand_2_out, nand_3_out, in_3);
  nand nand_7 (out_3, nand_1_out, nand_6_out);
  nand nand_8 (nand_8_out, in, in);
  nand nand_9 (nand_9_out, in_2, in_2);
  nand nand_10 (nand_10_out, A, nand_3_out, nand_8_out);
  nand nand_11 (out_2, nand_10_out, nand_9_out);
endmodule

module BCD_Comparer_6bit (
  input  [5:0] A,
  input  [5:0] B,
  output out_3,
  output out_4,
  output out_5
);

  wire compare_1bit_nand_1_out, compare_1bit_nand_1_out_2, compare_1bit_nand_1_out_3,
       compare_1bit_nand_2_out, compare_1bit_nand_2_out_2, compare_1bit_nand_2_out_3,
       compare_1bit_nand_3_out, compare_1bit_nand_3_out_2, compare_1bit_nand_3_out_3,
       compare_1bit_nand_4_out, compare_1bit_nand_4_out_2, compare_1bit_nand_4_out_3,
       compare_1bit_nand_5_out, compare_1bit_nand_5_out_2, compare_1bit_nand_5_out_3;

  COMPARE_1bit_NAND compare_1bit_nand_1 (
    .A(A[5]), .B(B[5]), .in(1'b0), .in_2(1'b0), .in_3(1'b1), .out(compare_1bit_nand_1_out),
    .out_2(compare_1bit_nand_1_out_2), .out_3(compare_1bit_nand_1_out_3));
  COMPARE_1bit_NAND compare_1bit_nand_2 (
    .A(A[4]), .B(B[4]), .in(compare_1bit_nand_1_out), .in_2(compare_1bit_nand_1_out_2),
    .in_3(compare_1bit_nand_1_out_3), .out(compare_1bit_nand_2_out), .out_2(compare_1bit_nand_2_out_2),
    .out_3(compare_1bit_nand_2_out_3));
  COMPARE_1bit_NAND compare_1bit_nand_3 (
    .A(A[3]), .B(B[3]), .in(compare_1bit_nand_2_out), .in_2(compare_1bit_nand_2_out_2),
    .in_3(compare_1bit_nand_2_out_3), .out(compare_1bit_nand_3_out), .out_2(compare_1bit_nand_3_out_2),
    .out_3(compare_1bit_nand_3_out_3));
  COMPARE_1bit_NAND compare_1bit_nand_4 (
    .A(A[2]), .B(B[2]), .in(compare_1bit_nand_3_out), .in_2(compare_1bit_nand_3_out_2),
    .in_3(compare_1bit_nand_3_out_3), .out(compare_1bit_nand_4_out), .out_2(compare_1bit_nand_4_out_2),
    .out_3(compare_1bit_nand_4_out_3));
  COMPARE_1bit_NAND compare_1bit_nand_5 (
    .A(A[1]), .B(B[1]), .in(compare_1bit_nand_4_out), .in_2(compare_1bit_nand_4_out_2),
    .in_3(compare_1bit_nand_4_out_3), .out(compare_1bit_nand_5_out), .out_2(compare_1bit_nand_5_out_2),
    .out_3(compare_1bit_nand_5_out_3));
  COMPARE_1bit_NAND compare_1bit_nand_6 (
    .A(A[0]), .B(B[0]), .in(compare_1bit_nand_5_out), .in_2(compare_1bit_nand_5_out_2),
    .in_3(compare_1bit_nand_5_out_3), .out(out_3), .out_2(out_4), .out_3(out_5));
endmodule

module BCD_Comparer_8bit_Zadatak4 (
  input  [7:0] A,
  input  [7:0] B
);

  wire compare_1bit_nor_1_jednakiout, compare_1bit_nor_1_xveceout, compare_1bit_nor_1_yveceout,
       compare_1bit_nor_2_jednakiout, compare_1bit_nor_2_xveceout, compare_1bit_nor_2_yveceout,
       compare_1bit_nor_3_jednakiout, compare_1bit_nor_3_xveceout, compare_1bit_nor_3_yveceout,
       compare_1bit_nor_4_jednakiout, compare_1bit_nor_4_xveceout, compare_1bit_nor_4_yveceout,
       compare_1bit_nor_5_jednakiout, compare_1bit_nor_5_xveceout, compare_1bit_nor_5_yveceout,
       compare_1bit_nor_6_jednakiout, compare_1bit_nor_6_xveceout, compare_1bit_nor_6_yveceout,
       compare_1bit_nor_7_jednakiout, compare_1bit_nor_7_xveceout, compare_1bit_nor_7_yveceout,
       compare_1bit_nor_8_jednakiout, compare_1bit_nor_8_xveceout, compare_1bit_nor_8_yveceout;

  // Probe on A
  // Probe on B
  LED A_jednako_B (.in(compare_1bit_nor_8_jednakiout));
  LED A_vece_od_B (.in(compare_1bit_nor_8_xveceout));
  LED B_vece_od_A (.in(compare_1bit_nor_8_yveceout));
  COMPARE_1bit_NOR compare_1bit_nor_1 (
    .x(A[7]), .y(B[7]), .yVeceIn(1'b0), .xVeceIn(1'b0), .jednakiIn(1'b1),
    .yVeceOut(compare_1bit_nor_1_yveceout), .xVeceOut(compare_1bit_nor_1_xveceout),
    .jednakiOut(compare_1bit_nor_1_jednakiout));
  COMPARE_1bit_NOR compare_1bit_nor_2 (
    .x(A[6]), .y(B[6]), .yVeceIn(compare_1bit_nor_1_yveceout), .xVeceIn(compare_1bit_nor_1_xveceout),
    .jednakiIn(compare_1bit_nor_1_jednakiout), .yVeceOut(compare_1bit_nor_2_yveceout),
    .xVeceOut(compare_1bit_nor_2_xveceout), .jednakiOut(compare_1bit_nor_2_jednakiout));
  COMPARE_1bit_NOR compare_1bit_nor_3 (
    .x(A[5]), .y(B[5]), .yVeceIn(compare_1bit_nor_2_yveceout), .xVeceIn(compare_1bit_nor_2_xveceout),
    .jednakiIn(compare_1bit_nor_2_jednakiout), .yVeceOut(compare_1bit_nor_3_yveceout),
    .xVeceOut(compare_1bit_nor_3_xveceout), .jednakiOut(compare_1bit_nor_3_jednakiout));
  COMPARE_1bit_NOR compare_1bit_nor_4 (
    .x(A[4]), .y(B[4]), .yVeceIn(compare_1bit_nor_3_yveceout), .xVeceIn(compare_1bit_nor_3_xveceout),
    .jednakiIn(compare_1bit_nor_3_jednakiout), .yVeceOut(compare_1bit_nor_4_yveceout),
    .xVeceOut(compare_1bit_nor_4_xveceout), .jednakiOut(compare_1bit_nor_4_jednakiout));
  COMPARE_1bit_NOR compare_1bit_nor_5 (
    .x(A[3]), .y(B[3]), .yVeceIn(compare_1bit_nor_4_yveceout), .xVeceIn(compare_1bit_nor_4_xveceout),
    .jednakiIn(compare_1bit_nor_4_jednakiout), .yVeceOut(compare_1bit_nor_5_yveceout),
    .xVeceOut(compare_1bit_nor_5_xveceout), .jednakiOut(compare_1bit_nor_5_jednakiout));
  COMPARE_1bit_NOR compare_1bit_nor_6 (
    .x(A[2]), .y(B[2]), .yVeceIn(compare_1bit_nor_5_yveceout), .xVeceIn(compare_1bit_nor_5_xveceout),
    .jednakiIn(compare_1bit_nor_5_jednakiout), .yVeceOut(compare_1bit_nor_6_yveceout),
    .xVeceOut(compare_1bit_nor_6_xveceout), .jednakiOut(compare_1bit_nor_6_jednakiout));
  COMPARE_1bit_NOR compare_1bit_nor_7 (
    .x(A[1]), .y(B[1]), .yVeceIn(compare_1bit_nor_6_yveceout), .xVeceIn(compare_1bit_nor_6_xveceout),
    .jednakiIn(compare_1bit_nor_6_jednakiout), .yVeceOut(compare_1bit_nor_7_yveceout),
    .xVeceOut(compare_1bit_nor_7_xveceout), .jednakiOut(compare_1bit_nor_7_jednakiout));
  COMPARE_1bit_NOR compare_1bit_nor_8 (
    .x(A[0]), .y(B[0]), .yVeceIn(compare_1bit_nor_7_yveceout), .xVeceIn(compare_1bit_nor_7_xveceout),
    .jednakiIn(compare_1bit_nor_7_jednakiout), .yVeceOut(compare_1bit_nor_8_yveceout),
    .xVeceOut(compare_1bit_nor_8_xveceout), .jednakiOut(compare_1bit_nor_8_jednakiout));
endmodule

module Zadatak1 (
  input  A,
  input  B,
  input  C
);

  wire xor_1_out, xor_2_out;

  xor xor_1 (xor_1_out, A, B);
  xor xor_2 (xor_2_out, xor_1_out, C);
  LED led_1 (.in(xor_2_out));

  // Notes on the sheet:
  //   Projektovati kolo koje ima tri ulaza a na izlazu se pali led dioda ako je broj jedinica na ulazu neparan. koriste se Osnovna kola. (Parcijalni 29.08.2018)
endmodule

module Zadatak2 (
  input  A,
  input  B,
  input  C,
  input  D,
  output Y3,
  output Y2,
  output Y1,
  output Y0
);

  not not_1 (Y3, A);
  not not_2 (Y2, B);
  not not_3 (Y1, C);
  not not_4 (Y0, D);

  // Notes on the sheet:
  //   EXCESS-3-BCD u 9 komplement
endmodule

module Zadatak3 (
  input  [2:0] x,
  input  [2:0] in_2,
  output [4:0] y,
  output [4:0] out_4
);

  wire and_2_out, and_3_out, and_4_out, and_5_out, and_6_out, and_7_out, and_8_out, and_9_out, and_10_out,
       and_11_out, not_1_out, not_2_out, not_3_out, not_4_out, not_5_out, not_6_out;

  // Probe on x
  not not_1 (not_1_out, x[2]);
  not not_2 (not_2_out, x[1]);
  not not_3 (not_3_out, x[0]);
  and and_1 (y[4], x[2], x[1]);
  and and_2 (and_2_out, not_1_out, x[1], x[0]);
  and and_3 (and_3_out, x[2], not_2_out);
  and and_4 (and_4_out, not_1_out, x[1], not_3_out);
  and and_5 (and_5_out, x[2], not_2_out);
  and and_6 (and_6_out, x[2], x[0]);
  and and_7 (and_7_out, not_2_out, x[0]);
  and and_8 (and_8_out, x[1], not_3_out);
  or or_1 (y[3], and_2_out, and_3_out);
  or or_2 (y[2], and_4_out, and_5_out, and_6_out);
  or or_3 (y[1], and_7_out, and_8_out);
  // Probe on {y[4:1], x[0]}
  // Probe on in_2
  not not_4 (not_4_out, in_2[0]);
  not not_5 (not_5_out, in_2[1]);
  not not_6 (not_6_out, in_2[2]);
  or or_4 (out_4[2], in_2[2], and_9_out);
  and and_9 (and_9_out, not_4_out, in_2[1]);
  and and_10 (and_10_out, in_2[2], not_5_out);
  or or_5 (out_4[3], and_10_out, and_11_out);
  and and_11 (and_11_out, in_2[0], in_2[1], not_6_out);
  and and_12 (out_4[4], in_2[1], in_2[2]);
  xor xor_1 (out_4[1], in_2[1], in_2[0]);
  // Probe on {out_4[4:1], in_2[0]}

  assign out_4[0] = in_2[0];
  assign y[0] = x[0];

  // Notes on the sheet:
  //   Projektovati sklop koji na ulazu prima trobitni broj i realizuje y=3x
endmodule

module Zadatak4 (
  input  [2:0] x,
  output [3:0] y
);

  wire decoder_1_out0, decoder_1_out1, decoder_1_out2, decoder_1_out3, decoder_1_out4, decoder_1_out5,
       decoder_1_out6, decoder_1_out7;

  Decoder #(.select(3)) decoder_1 (
    .out0(decoder_1_out0), .out1(decoder_1_out1), .out2(decoder_1_out2), .out3(decoder_1_out3),
    .out4(decoder_1_out4), .out5(decoder_1_out5), .out6(decoder_1_out6), .out7(decoder_1_out7), .sel(x));  // open: en
  or or_1 (y[2], decoder_1_out4, decoder_1_out5, decoder_1_out6, decoder_1_out7);
  or or_2 (y[1], decoder_1_out2, decoder_1_out3, decoder_1_out6, decoder_1_out7);
  or or_3 (y[0], decoder_1_out1, decoder_1_out3, decoder_1_out5, decoder_1_out7);

  assign y[3] = 1'b0;

  // Notes on the sheet:
  //   Projektovati ROM kapaciteta 8 adresa numerisanih redom od 0 do 7. Na svakoj adresi je napisana njena vvrijednost u 2kk.
endmodule

module Zadatak5 (
  input  A,
  input  B,
  output Y0,
  output Y1,
  output Y2,
  output Y3
);

  wire not_1_out;

  // Probe on {A, B}
  not not_1 (not_1_out, B);
  and AB_2 (Y2, A, not_1_out);
  and AB (Y3, A, B);
  // Probe on {Y3, Y2, 1'b0, B}

  assign Y0 = B;
  assign Y1 = 1'b0;

  // Notes on the sheet:
  //   Ulaz prima dvobitni neoznaceni broj a na izlazu daje kvadrat tog broja 
endmodule

module Zadatak6 (
  input  A,
  input  B,
  input  C,
  output Y5,
  output Y4,
  output Y3,
  output Y2,
  output Y1,
  output Y0
);

  wire and_2_out, and_3_out, and_4_out, and_5_out, not_1_out, not_2_out, not_3_out, not_4_out;

  // Probe on {A, B, C}
  and and_1 (Y5, A, B);
  not not_1 (not_1_out, B);
  not not_2 (not_2_out, A);
  not not_3 (not_3_out, B);
  not not_4 (not_4_out, C);
  and and_2 (and_2_out, A, not_1_out);
  and and_3 (and_3_out, A, C);
  and and_4 (and_4_out, not_2_out, B, C);
  and and_5 (and_5_out, A, not_3_out, C);
  and and_6 (Y2, B, not_4_out);
  or or_1 (Y4, and_2_out, and_3_out);
  or or_2 (Y3, and_4_out, and_5_out);
  // Probe on {Y5, Y4, Y3, Y2, 1'b0, C}

  assign Y0 = C;
  assign Y1 = 1'b0;

  // Notes on the sheet:
  //   Ulaz prima dvobitni neoznaceni broj a na izlazu daje kvadrat tog broja 
endmodule

module Zadatak7 (
  input  A,
  input  B,
  input  C,
  input  D,
  output Y3,
  output Y2,
  output Y1,
  output Y0
);

  wire and_1_out, and_2_out, and_3_out, and_4_out, and_5_out, and_6_out, and_7_out, not_1_out, not_2_out,
       not_3_out, not_4_out;

  // Probe on {D, C, B, A}
  not not_1 (not_1_out, A);
  not not_2 (not_2_out, B);
  not not_3 (not_3_out, C);
  not not_4 (not_4_out, D);
  and and_1 (and_1_out, not_1_out, C);
  and and_2 (and_2_out, A, not_3_out, D);
  and and_3 (and_3_out, C, not_4_out);
  and and_4 (and_4_out, B, not_3_out, not_4_out);
  and and_5 (and_5_out, not_1_out, B);
  and and_6 (and_6_out, not_2_out, A, D);
  and and_7 (and_7_out, A, not_2_out, C);
  or or_1 (Y1, and_1_out, and_2_out, and_3_out);
  or or_2 (Y2, and_4_out, and_5_out, and_6_out, and_7_out);
  // Probe on {A, Y2, Y1, D}

  assign Y0 = D;
  assign Y3 = A;

  // Notes on the sheet:
  //   4bit 2kk izlaz znak-vrijednost
endmodule

module Zadatak8 (
  input  A,
  input  B,
  input  C,
  input  D,
  output Y3,
  output Y2,
  output Y1,
  output Y0
);

  wire and_1_out, and_2_out, and_3_out, and_4_out, and_5_out, not_1_out, not_2_out;

  not not_1 (not_1_out, B);
  not not_2 (not_2_out, C);
  not not_3 (Y0, D);
  and and_1 (and_1_out, B, D);
  and and_2 (and_2_out, B, C);
  xnor xnor_1 (Y1, C, D);
  and and_3 (and_3_out, C, not_1_out);
  and and_4 (and_4_out, D, not_1_out);
  and and_5 (and_5_out, Y0, not_2_out, B);
  or or_1 (Y3, A, and_1_out, and_2_out);
  or or_2 (Y2, and_3_out, and_4_out, and_5_out);

  // Notes on the sheet:
  //   konverter BCD u Excess-3-BCD kod
endmodule

module Zadatak9 (
  input  [3:0] in_1
);

  wire decoder_1_out0, decoder_1_out1, decoder_1_out2, decoder_1_out3, decoder_1_out4, decoder_1_out5,
       decoder_1_out6, decoder_1_out7, decoder_1_out8, decoder_1_out9, decoder_1_out10, decoder_1_out11,
       decoder_1_out12, decoder_1_out13, decoder_1_out14, decoder_1_out15, or_1_out, or_2_out, or_3_out,
       or_4_out, or_5_out, or_6_out, or_7_out;

  Decoder #(.enable("false"), .select(4)) decoder_1 (
    .out0(decoder_1_out0), .out1(decoder_1_out1), .out2(decoder_1_out2), .out3(decoder_1_out3),
    .out4(decoder_1_out4), .out5(decoder_1_out5), .out6(decoder_1_out6), .out7(decoder_1_out7),
    .out8(decoder_1_out8), .out9(decoder_1_out9), .out10(decoder_1_out10), .out11(decoder_1_out11),
    .out12(decoder_1_out12), .out13(decoder_1_out13), .out14(decoder_1_out14), .out15(decoder_1_out15),
    .sel(in_1));
  or or_1 (or_1_out, decoder_1_out0, decoder_1_out2, decoder_1_out3, decoder_1_out14, decoder_1_out5, decoder_1_out6, decoder_1_out7, decoder_1_out8, decoder_1_out9, decoder_1_out10, decoder_1_out12, decoder_1_out15);
  _7_Segment_Display u_7_segment_display_1 (
    .g(or_7_out), .f(or_6_out), .a(or_1_out), .b(or_2_out), .e(or_5_out), .d(or_4_out), .c(or_3_out));  // open: dp
  or or_2 (or_2_out, decoder_1_out0, decoder_1_out1, decoder_1_out2, decoder_1_out3, decoder_1_out4, decoder_1_out7, decoder_1_out8, decoder_1_out9, decoder_1_out10, decoder_1_out13);
  or or_3 (or_3_out, decoder_1_out0, decoder_1_out1, decoder_1_out3, decoder_1_out4, decoder_1_out5, decoder_1_out6, decoder_1_out7, decoder_1_out8, decoder_1_out9, decoder_1_out10, decoder_1_out11, decoder_1_out13);
  or or_4 (or_4_out, decoder_1_out0, decoder_1_out2, decoder_1_out3, decoder_1_out5, decoder_1_out6, decoder_1_out8, decoder_1_out9, decoder_1_out11, decoder_1_out12, decoder_1_out13, decoder_1_out14);
  or or_5 (or_5_out, decoder_1_out0, decoder_1_out10, decoder_1_out2, decoder_1_out6, decoder_1_out8, decoder_1_out11, decoder_1_out12, decoder_1_out13, decoder_1_out14, decoder_1_out15);
  or or_6 (or_6_out, decoder_1_out0, decoder_1_out4, decoder_1_out5, decoder_1_out6, decoder_1_out8, decoder_1_out9, decoder_1_out10, decoder_1_out11, decoder_1_out12, decoder_1_out14, decoder_1_out15);
  or or_7 (or_7_out, decoder_1_out2, decoder_1_out3, decoder_1_out4, decoder_1_out5, decoder_1_out6, decoder_1_out8, decoder_1_out9, decoder_1_out10, decoder_1_out11, decoder_1_out13, decoder_1_out14, decoder_1_out15);

  // Notes on the sheet:
  //   Predstaviti 4bit Hexadecimalni broj preko 7segmentnog displeya
endmodule

module Zadatak10 (
  input  [2:0] Adresa,
  output [3:0] Podatak
);

  wire decoder_1_out0, decoder_1_out1, decoder_1_out2, decoder_1_out3, decoder_1_out4, decoder_1_out5,
       decoder_1_out6, decoder_1_out7;

  Decoder #(.enable("false"), .select(3)) decoder_1 (
    .out0(decoder_1_out0), .out1(decoder_1_out1), .out2(decoder_1_out2), .out3(decoder_1_out3),
    .out4(decoder_1_out4), .out5(decoder_1_out5), .out6(decoder_1_out6), .out7(decoder_1_out7), .sel(Adresa));
  or or_1 (Podatak[3], decoder_1_out0, decoder_1_out1, decoder_1_out5);
  or or_2 (Podatak[2], decoder_1_out3, decoder_1_out7);
  // Probe on Podatak
  or or_3 (Podatak[1], decoder_1_out1, decoder_1_out7);
  or or_4 (Podatak[0], decoder_1_out0, decoder_1_out7);

  // Notes on the sheet:
  //   9, 10, 0, 4, 0, 8, 0, 7
endmodule

module Zadatak11 (
  input  A,
  input  B,
  input  C,
  output out_4
);

  wire xor_1_out;

  xor xor_1 (xor_1_out, A, B);
  // XOR_Gate xor_2 has open pins: in0=xor_1_out, in1=C, out=open
  xnor xnor_1 (out_4, xor_1_out, C);

  // Notes on the sheet:
  //   XOR tri ulaza tacno ako je paran broj na ulazu
endmodule

module Zadatak12 (
  input  A,
  input  B,
  input  C,
  output Y
);

  wire and_1_out, and_2_out, and_3_out, and_4_out, not_1_out, not_2_out, not_3_out;

  not not_1 (not_1_out, A);
  not not_2 (not_2_out, B);
  not not_3 (not_3_out, C);
  and and_1 (and_1_out, not_1_out, not_2_out, not_3_out);
  and and_2 (and_2_out, not_1_out, B, C);
  and and_3 (and_3_out, A, not_2_out, C);
  and and_4 (and_4_out, A, B, not_3_out);
  or or_1 (Y, and_1_out, and_2_out, and_3_out, and_4_out);

  // Notes on the sheet:
  //   tri ulaza, izlaz 1 tacno ako je paran broj na ulazu
  //      A' B' C'
  //   A' B C
  //   A B' C
  //   A B C'
endmodule

module Zadatak13 (
  input  [3:0] in_1
);

  wire decoder_1_out0, decoder_1_out1, decoder_1_out2, decoder_1_out3, decoder_1_out4, decoder_1_out5,
       decoder_1_out6, decoder_1_out7, decoder_1_out8, decoder_1_out9, or_1_out, or_2_out, or_3_out,
       or_4_out, or_5_out, or_6_out, or_7_out;

  Decoder #(.enable("false"), .select(4)) decoder_1 (
    .out0(decoder_1_out0), .out1(decoder_1_out1), .out2(decoder_1_out2), .out3(decoder_1_out3),
    .out4(decoder_1_out4), .out5(decoder_1_out5), .out6(decoder_1_out6), .out7(decoder_1_out7),
    .out8(decoder_1_out8), .out9(decoder_1_out9), .sel(in_1));  // open: out10, out11, out12, out13, out14, out15
  or or_1 (or_1_out, decoder_1_out0, decoder_1_out2, decoder_1_out3, decoder_1_out5, decoder_1_out6, decoder_1_out7, decoder_1_out8, decoder_1_out9);
  or or_2 (or_2_out, decoder_1_out0, decoder_1_out1, decoder_1_out2, decoder_1_out3, decoder_1_out4, decoder_1_out7, decoder_1_out8, decoder_1_out9);
  or or_3 (or_3_out, decoder_1_out0, decoder_1_out1, decoder_1_out3, decoder_1_out4, decoder_1_out5, decoder_1_out6, decoder_1_out7, decoder_1_out8, decoder_1_out9);
  or or_4 (or_4_out, decoder_1_out0, decoder_1_out2, decoder_1_out3, decoder_1_out5, decoder_1_out6, decoder_1_out8, decoder_1_out9);
  _7_Segment_Display u_7_segment_display_1 (
    .g(or_7_out), .f(or_6_out), .a(or_1_out), .b(or_2_out), .e(or_5_out), .d(or_4_out), .c(or_3_out));  // open: dp
  or or_5 (or_5_out, decoder_1_out0, decoder_1_out2, decoder_1_out6, decoder_1_out8);
  or or_6 (or_6_out, decoder_1_out0, decoder_1_out4, decoder_1_out5, decoder_1_out6, decoder_1_out8, decoder_1_out9);
  or or_7 (or_7_out, decoder_1_out2, decoder_1_out3, decoder_1_out4, decoder_1_out5, decoder_1_out6, decoder_1_out8, decoder_1_out9);

  // Notes on the sheet:
  //   Predstaviti 4bit Binarni broj preko 7segmentnog displeya
endmodule

module Zadatak14 (
  input  A,
  input  B,
  input  C,
  input  D,
  output I
);

  wire and_1_out, and_2_out, and_3_out, and_4_out, not_1_out, not_2_out, not_3_out, not_4_out;

  not not_1 (not_1_out, A);
  not not_2 (not_2_out, B);
  not not_3 (not_3_out, C);
  not not_4 (not_4_out, D);
  and and_1 (and_1_out, not_1_out, not_2_out, not_3_out);
  and and_2 (and_2_out, not_1_out, not_2_out, not_4_out);
  and and_3 (and_3_out, not_1_out, not_3_out, not_4_out);
  and and_4 (and_4_out, not_2_out, not_3_out, not_4_out);
  or or_1 (I, and_1_out, and_2_out, and_3_out, and_4_out);

  // Notes on the sheet:
  //   4 ulaza, izlaz je 0 ako je broj jedinica na ulazima dva ili vise
endmodule

module Zadatak15 (
  input  [2:0] A,
  input  [2:0] B,
  output [2:0] Rez,
  output [2:0] Cout
);

  wire comparator_1_eq;
  wire [2:0] adder_1_out, multiplier_1_cout, multiplier_1_out;

  // Probe on A
  // Probe on B
  Multiplier #(.mode("twosComplement"), .width(3)) multiplier_1 (
    .a(A), .b(B), .out(multiplier_1_out), .cout(multiplier_1_cout));  // open: cin
  Adder #(.width(3)) adder_1 (.a(A), .b(B), .out(adder_1_out), .cin(1'b0));  // open: cout
  Comparator #(.width(3)) comparator_1 (.a(adder_1_out), .b(3'b001), .eq(comparator_1_eq));  // open: gt, lt
  Multiplexer #(.width(3)) multiplexer_1 (.in0(3'b000), .in1(multiplier_1_cout), .out(Cout), .sel(comparator_1_eq));
  Multiplexer #(.width(3)) multiplexer_2 (.in0(3'b000), .in1(multiplier_1_out), .out(Rez), .sel(comparator_1_eq));

  // Notes on the sheet:
  //   Ulaz su 3bit A i B ako je A+B=1 radi se množenje ova dva broja (znaci validno za -1 i 2 ili)
endmodule

module NOT_preko_NOR (
  input  A,
  output R
);

  nor nor_1 (R, A, A);
endmodule

module OR_preko_NOR (
  input  A,
  input  B,
  output R
);

  wire nor_1_out;

  nor nor_1 (nor_1_out, A, B);
  nor nor_2 (R, nor_1_out, nor_1_out);
endmodule

module AND_preko_NOR (
  input  A,
  input  B,
  output R
);

  wire nor_1_out, nor_2_out;

  nor nor_1 (nor_1_out, A, A);
  nor nor_2 (nor_2_out, B, B);
  nor nor_3 (R, nor_1_out, nor_2_out);
endmodule

module NAND_preko_NOR (
  input  A,
  input  B,
  output R
);

  wire nor_1_out, nor_2_out, nor_3_out;

  nor nor_1 (nor_1_out, A, A);
  nor nor_2 (nor_2_out, B, B);
  nor nor_3 (nor_3_out, nor_1_out, nor_2_out);
  nor nor_4 (R, nor_3_out, nor_3_out);
endmodule

module XOR_preko_NOR (
  input  A,
  input  B,
  output R
);

  wire nor_1_out, nor_2_out, nor_3_out, nor_4_out;

  nor nor_1 (nor_1_out, A, B);
  nor nor_2 (nor_2_out, A, nor_1_out);
  nor nor_3 (nor_3_out, nor_1_out, B);
  nor nor_4 (nor_4_out, nor_2_out, nor_3_out);
  nor nor_5 (R, nor_4_out, nor_4_out);
endmodule
