// Logisim project IParcZadatak_1_EmanAlibalić.circ as structural Verilog: 1 circuit, main circuit main
module main (
  input  [3:0] A,
  output [3:0] I
);

  wire and_2_out, and_3_out, and_4_out, and_5_out, and_6_out, and_7_out, and_8_out, and_9_out, and_10_out,
       and_11_out, and_12_out, and_13_out, and_14_out, and_15_out, not_1_out, not_2_out, not_3_out, not_4_out;

  not not_1 (not_1_out, A[3]);
  not not_2 (not_2_out, A[2]);
  not not_3 (not_3_out, A[1]);
  not not_4 (not_4_out, A[0]);
  and and_1 (I[3], not_1_out, not_2_out, not_3_out, not_4_out);
  or or_1 (I[2], A[0], A[1], A[2], A[3]);
  and and_2 (and_2_out, not_1_out, not_2_out, A[0]);
  and and_3 (and_3_out, A[2], not_4_out);
  and and_4 (and_4_out, A[3], not_4_out);
  and and_5 (and_5_out, A[3], A[2]);
  and and_6 (and_6_out, not_1_out, not_2_out, A[1]);
  and and_7 (and_7_out, not_1_out, not_2_out, A[1], not_4_out);
  and and_8 (and_8_out, not_1_out, not_3_out, A[0]);
  and and_9 (and_9_out, not_1_out, A[2], not_3_out);
  and and_10 (and_10_out, not_1_out, A[2], A[0]);
  and and_11 (and_11_out, A[3], not_2_out, not_3_out);
  and and_12 (and_12_out, A[3], not_2_out, A[0]);
  and and_13 (and_13_out, A[2], not_3_out, not_4_out);
  and and_14 (and_14_out, A[3], A[2], not_4_out);
  and and_15 (and_15_out, A[2], A[1], A[0]);
  or or_2 (I[1], and_2_out, and_3_out, and_4_out, and_5_out, and_6_out);
  or or_3 (I[0], and_7_out, and_8_out, and_9_out, and_10_out, and_11_out, and_12_out, and_13_out, and_14_out, and_15_out);
endmodule
