// Logisim project IParcZadatak_2_EmanAlibalić.circ as structural Verilog: 6 circuits, main circuit ADD_1bit
module ADD_1bit (
  input  A,
  input  B,
  input  Cin,
  output S,
  output Cout
);

  wire and_1_out, not_1_out, or_1_out, xor_1_out;

  xor xor_1 (xor_1_out, A, B);
  not not_1 (not_1_out, xor_1_out);
  and and_1 (and_1_out, A, B);
  or or_1 (or_1_out, B, A);
  Multiplexer multiplexer_1 (.in0(xor_1_out), .in1(not_1_out), .out(S), .sel(Cin));
  Multiplexer multiplexer_2 (.in0(and_1_out), .in1(or_1_out), .out(Cout), .sel(Cin));
endmodule

module SUBTRACT_1bit (
  input  c,
  input  a,
  input  b,
  output rez,
  output carry
);

  wire and_1_out, and_2_out, and_3_out, and_4_out, and_5_out, and_6_out, and_7_out, not_1_out, not_2_out,
       not_3_out;

  not not_1 (not_1_out, c);
  not not_2 (not_2_out, a);
  not not_3 (not_3_out, b);
  and and_1 (and_1_out, not_1_out, not_2_out, b);
  and and_2 (and_2_out, not_1_out, a, not_3_out);
  and and_3 (and_3_out, c, not_2_out, not_3_out);
  and and_4 (and_4_out, c, a, b);
  and and_5 (and_5_out, not_2_out, b);
  and and_6 (and_6_out, c, not_2_out);
  and and_7 (and_7_out, c, b);
  or or_1 (rez, and_1_out, and_2_out, and_3_out, and_4_out);
  or or_2 (carry, and_5_out, and_6_out, and_7_out);
endmodule

module NOT_preko_MUX (
  input  in_1,
  output out_2
);

  Multiplexer #(.select(2)) multiplexer_1 (.in0(1'b1), .in1(1'b0), .out(out_2), .sel({1'b0, in_1}));  // open: in2, in3
endmodule

module AB_1bit (
  input  A,
  input  B,
  output REZ
);

  wire nand_1_out, nand_2_out;

  nand nand_1 (nand_1_out, 1'b1, A);
  nand nand_2 (nand_2_out, 1'b1, B);
  nand nand_3 (REZ, nand_2_out, nand_1_out);
endmodule

module ALU_1bit (
  input  Cin,
  input  A,
  input  [1:0] F,
  input  B,
  output C,
  output R
);

  wire ab_1bit_1_rez, add_1bit_1_s, and_1_out, not_preko_mux_1_out_2, not_preko_mux_2_out_2;

  and and_1 (and_1_out, B, A);
  ADD_1bit add_1bit_1 (.A(B), .B(A), .Cin(Cin), .S(add_1bit_1_s), .Cout(C));
  NOT_preko_MUX not_preko_mux_1 (.in_1(B), .out_2(not_preko_mux_1_out_2));
  AB_1bit ab_1bit_1 (.A(B), .B(A), .REZ(ab_1bit_1_rez));
  NOT_preko_MUX not_preko_mux_2 (.in_1(add_1bit_1_s), .out_2(not_preko_mux_2_out_2));
  Multiplexer #(.select(2)) multiplexer_1 (
    .in0(not_preko_mux_2_out_2), .in1(not_preko_mux_1_out_2), .in2(and_1_out), .in3(ab_1bit_1_rez), .out(R),
    .sel(F));
endmodule

module ALU6bit_ZADATAK2 (
  input  [1:0] F,
  input  [5:0] A,
  input  [5:0] B,
  output [5:0] Rez
);

  wire c1, c2, c3, c4, c5, c6;

  ALU_1bit alu_1bit_1 (.Cin(1'b0), .A(A[0]), .F(F), .B(B[0]), .C(c1), .R(Rez[0]));
  ALU_1bit alu_1bit_2 (.Cin(c1), .A(A[1]), .F(F), .B(B[1]), .C(c2), .R(Rez[1]));
  ALU_1bit alu_1bit_3 (.Cin(c2), .A(A[2]), .F(F), .B(B[2]), .C(c3), .R(Rez[2]));
  ALU_1bit alu_1bit_4 (.Cin(c3), .A(A[3]), .F(F), .B(B[3]), .C(c4), .R(Rez[3]));
  ALU_1bit alu_1bit_5 (.Cin(c4), .A(A[4]), .F(F), .B(B[4]), .C(c5), .R(Rez[4]));
  ALU_1bit alu_1bit_6 (.Cin(c5), .A(A[5]), .F(F), .B(B[5]), .C(c6), .R(Rez[5]));
endmodule
