// Logisim project Poredjenje.circ as structural Verilog: 2 circuits, main circuit COMPARE_1bit_NOR
module COMPARE_1bit_NOR (
  input  x,
  input  y,
  input  yVeceIn,
  input  xVeceIn,
  input  jednakiIn,
  output yVeceOut,
  output xVeceOut,
  output jednakiOut
);

  wire nor_6_out, nor_7_out, nor_8_out, nor_9_out, nor_10_out, nor_11_out, nor_12_out, nor_13_out, notCase1,
       notCase2, notCase3, notX, notY;

  nor nor_1 (notX, x, x);
  nor nor_2 (notY, y, y);
  nor nor_3 (notCase1, yVeceIn, yVeceIn);
  nor nor_4 (notCase2, xVeceIn, xVeceIn);
  nor nor_5 (notCase3, jednakiIn, jednakiIn);
  nor nor_6 (nor_6_out, notX, yVeceIn);
  nor nor_7 (nor_7_out, notY, xVeceIn);
  nor nor_8 (nor_8_out, y, notX);
  nor nor_9 (nor_9_out, y, yVeceIn);
  nor nor_10 (nor_10_out, yVeceIn, notCase2);
  nor nor_11 (nor_11_out, x, xVeceIn);
  nor nor_12 (nor_12_out, notCase1, xVeceIn);
  nor nor_13 (nor_13_out, x, notY);
  nor nor_14 (yVeceOut, nor_9_out, nor_10_out, nor_6_out);
  nor nor_15 (xVeceOut, nor_11_out, nor_12_out, nor_7_out);
  nor nor_16 (jednakiOut, notCase3, nor_13_out, nor_8_out);

  // Other names for the same wires on the sheet: Case1 = yVeceIn; Case2 = xVeceIn; Case3 = jednakiIn
endmodule

module Comparer_8bit (
  input  [7:0] A,
  input  [7:0] B,
  output [1:0] Y
);

  wire compare_1bit_nor_1_jednakiout, compare_1bit_nor_1_xveceout, compare_1bit_nor_1_yveceout,
       compare_1bit_nor_2_jednakiout, compare_1bit_nor_2_xveceout, compare_1bit_nor_2_yveceout,
       compare_1bit_nor_3_jednakiout, compare_1bit_nor_3_xveceout, compare_1bit_nor_3_yveceout,
       compare_1bit_nor_4_jednakiout, compare_1bit_nor_4_xveceout, compare_1bit_nor_4_yveceout,
       compare_1bit_nor_5_jednakiout, compare_1bit_nor_5_xveceout, compare_1bit_nor_5_yveceout,
       compare_1bit_nor_6_jednakiout, compare_1bit_nor_6_xveceout, compare_1bit_nor_6_yveceout,
       compare_1bit_nor_7_jednakiout, compare_1bit_nor_7_xveceout, compare_1bit_nor_7_yveceout,
       compare_1bit_nor_8_jednakiout;

  // Probe on A
  // Probe on B
  COMPARE_1bit_NOR compare_1bit_nor_1 (
    .x(A[7]), .y(B[7]), .yVeceIn(1'b0), .xVeceIn(1'b0), .jednakiIn(1'b1),
    .yVeceOut(compare_1bit_nor_1_yveceout), .xVeceOut(compare_1bit_nor_1_xveceout),
    .jednakiOut(compare_1bit_nor_1_jednakiout));
  COMPARE_1bit_NOR compare_1bit_nor_2 (
    .x(A[6]), .y(B[6]), .yVeceIn(compare_1bit_nor_1_yveceout), .xVeceIn(compare_1bit_nor_1_xveceout),
    .jednakiIn(compare_1bit_nor_1_jednakiout), .yVeceOut(compare_1bit_nor_2_yveceout),
    .xVeceOut(compare_1bit_nor_2_xveceout), .jednakiOut(compare_1bit_nor_2_jednakiout));
  COMPARE_1bit_NOR compare_1bit_nor_3 (
    .x(A[5]), .y(B[5]), .yVeceIn(compare_1bit_nor_2_yveceout), .xVeceIn(compare_1bit_nor_2_xveceout),
    .jednakiIn(compare_1bit_nor_2_jednakiout), .yVeceOut(compare_1bit_nor_3_yveceout),
    .xVeceOut(compare_1bit_nor_3_xveceout), .jednakiOut(compare_1bit_nor_3_jednakiout));
  COMPARE_1bit_NOR compare_1bit_nor_4 (
    .x(A[4]), .y(B[4]), .yVeceIn(compare_1bit_nor_3_yveceout), .xVeceIn(compare_1bit_nor_3_xveceout),
    .jednakiIn(compare_1bit_nor_3_jednakiout), .yVeceOut(compare_1bit_nor_4_yveceout),
    .xVeceOut(compare_1bit_nor_4_xveceout), .jednakiOut(compare_1bit_nor_4_jednakiout));
  COMPARE_1bit_NOR compare_1bit_nor_5 (
    .x(A[3]), .y(B[3]), .yVeceIn(compare_1bit_nor_4_yveceout), .xVeceIn(compare_1bit_nor_4_xveceout),
    .jednakiIn(compare_1bit_nor_4_jednakiout), .yVeceOut(compare_1bit_nor_5_yveceout),
    .xVeceOut(compare_1bit_nor_5_xveceout), .jednakiOut(compare_1bit_nor_5_jednakiout));
  COMPARE_1bit_NOR compare_1bit_nor_6 (
    .x(A[2]), .y(B[2]), .yVeceIn(compare_1bit_nor_5_yveceout), .xVeceIn(compare_1bit_nor_5_xveceout),
    .jednakiIn(compare_1bit_nor_5_jednakiout), .yVeceOut(compare_1bit_nor_6_yveceout),
    .xVeceOut(compare_1bit_nor_6_xveceout), .jednakiOut(compare_1bit_nor_6_jednakiout));
  COMPARE_1bit_NOR compare_1bit_nor_7 (
    .x(A[1]), .y(B[1]), .yVeceIn(compare_1bit_nor_6_yveceout), .xVeceIn(compare_1bit_nor_6_xveceout),
    .jednakiIn(compare_1bit_nor_6_jednakiout), .yVeceOut(compare_1bit_nor_7_yveceout),
    .xVeceOut(compare_1bit_nor_7_xveceout), .jednakiOut(compare_1bit_nor_7_jednakiout));
  COMPARE_1bit_NOR compare_1bit_nor_8 (
    .x(A[0]), .y(B[0]), .yVeceIn(compare_1bit_nor_7_yveceout), .xVeceIn(compare_1bit_nor_7_xveceout),
    .jednakiIn(compare_1bit_nor_7_jednakiout), .yVeceOut(Y[0]), .xVeceOut(Y[1]),
    .jednakiOut(compare_1bit_nor_8_jednakiout));
endmodule
