// Logisim project Eman_Alibalic_II_Parcijala_Zadatak.circ as structural Verilog: 2 circuits, main circuit main
module main (
  input  in_1,
  output out_2
);

  wire brojac_cifara_1_out_2, clock_1_out, d_ff_1_q, d_ff_2_q, d_ff_3_q, or_1_out;

  Clock clock_1 (.out(clock_1_out));
  D_Flip_Flop d_ff_1 (.D(in_1), .clk(clock_1_out), .Q(d_ff_1_q));  // open: Qn, preset, reset
  brojac_cifara brojac_cifara_1 (.clock(clock_1_out), .out_2(brojac_cifara_1_out_2));
  D_Flip_Flop d_ff_2 (.D(d_ff_1_q), .clk(clock_1_out), .Q(d_ff_2_q));  // open: Qn, preset, reset
  D_Flip_Flop d_ff_3 (.D(d_ff_2_q), .clk(clock_1_out), .Q(d_ff_3_q));  // open: Qn, preset, reset
  // Probe on brojac_cifara_1_out_2
  or or_1 (or_1_out, d_ff_3_q, d_ff_2_q, d_ff_1_q);
  and and_1 (out_2, or_1_out, brojac_cifara_1_out_2);
endmodule

module brojac_cifara (
  input  clock,
  output out_2
);

  wire or_1_out, T0_q, T1_q;

  T_Flip_Flop T1 (.T(T0_q), .clk(clock), .Q(T1_q));  // open: Qn, reset, preset
  T_Flip_Flop T0 (.T(or_1_out), .clk(clock), .Q(T0_q));  // open: Qn, reset, preset
  or or_1 (or_1_out, ~T1_q, ~T0_q);  // OR_Gate
  and and_1 (out_2, T0_q, T1_q);
endmodule
