// Logisim project funky brojač.circ as structural Verilog: 3 circuits, main circuit main
module main (
  input  in_1
);

  wire brojac_cifara_1_out_2, clock_1_out, d_ff_1_q, d_ff_2_q, d_ff_3_q;
  wire [2:0] brojac_07_1_out_5;

  Clock clock_1 (.out(clock_1_out));
  D_Flip_Flop d_ff_1 (.D(in_1), .clk(clock_1_out), .Q(d_ff_1_q));  // open: Qn, preset, reset
  D_Flip_Flop d_ff_2 (.D(d_ff_1_q), .clk(clock_1_out), .Q(d_ff_2_q));  // open: Qn, preset, reset
  D_Flip_Flop d_ff_3 (.D(d_ff_2_q), .clk(clock_1_out), .Q(d_ff_3_q));  // open: Qn, preset, reset
  brojac_cifara brojac_cifara_1 (.clock(clock_1_out), .out_2(brojac_cifara_1_out_2));
  brojac_07 brojac_07_1 (
    .x(d_ff_3_q), .clck(brojac_cifara_1_out_2), .out_3(brojac_07_1_out_5[2]), .out_4(brojac_07_1_out_5[1]),
    .out_5(brojac_07_1_out_5[0]));
  // Probe on brojac_07_1_out_5
endmodule

module brojac_cifara (
  input  clock,
  output out_2
);

  wire or_1_out, T0_q, T1_q;

  T_Flip_Flop T1 (.T(T0_q), .clk(clock), .Q(T1_q));  // open: Qn, reset, preset
  T_Flip_Flop T0 (.T(or_1_out), .clk(clock), .Q(T0_q));  // open: Qn, reset, preset
  or or_1 (or_1_out, ~T1_q, ~T0_q);  // OR_Gate
  and and_1 (out_2, T0_q, T1_q);
endmodule

module brojac_07 (
  input  x,
  input  clck,
  output out_3,
  output out_4,
  output out_5
);

  wire and_1_out, and_2_out, and_3_out, and_4_out, and_5_out, and_6_out, and_7_out, and_8_out, and_9_out,
       and_10_out, and_11_out, and_12_out, and_13_out, k0, k1, k2, not_1_out, not_2_out, not_3_out;

  not not_1 (not_1_out, out_4);
  not not_2 (not_2_out, out_5);
  not not_3 (not_3_out, x);
  and and_1 (and_1_out, out_4, out_5, not_3_out);
  and and_2 (and_2_out, out_3, not_3_out);
  and and_3 (and_3_out, out_3, out_5);
  and and_4 (and_4_out, out_3, out_4);
  and and_5 (and_5_out, not_1_out, out_5, not_3_out);
  and and_6 (and_6_out, out_4, not_2_out, not_3_out);
  and and_7 (and_7_out, out_4, out_5, x);
  and and_8 (and_8_out, out_3, not_1_out, not_2_out, x);
  and and_9 (and_9_out, out_3, out_5, not_3_out);
  and and_10 (and_10_out, not_2_out, not_3_out);
  and and_11 (and_11_out, out_4, not_2_out);
  and and_12 (and_12_out, out_3, not_2_out);
  and and_13 (and_13_out, out_3, out_4, not_3_out);
  or or_1 (k0, and_1_out, and_2_out, and_3_out, and_4_out);
  or or_2 (k1, and_5_out, and_6_out, and_7_out, and_8_out, and_9_out);
  or or_3 (k2, and_10_out, and_11_out, and_12_out, and_13_out);
  D_Flip_Flop d_ff_1 (.D(k0), .clk(clck), .Q(out_3));  // open: Qn, preset, reset
  D_Flip_Flop d_ff_2 (.D(k1), .clk(clck), .Q(out_4));  // open: Qn, preset, reset
  D_Flip_Flop d_ff_3 (.D(k2), .clk(clck), .Q(out_5));  // open: Qn, preset, reset

  // Other names for the same wires on the sheet: q0 = out_3; q1 = out_4; q2 = out_5
endmodule
