// Logisim project ZadatakSemafor.circ as structural Verilog
module Semafor_main (
  input  x,
  output crveno,
  output zuto,
  output zeleno,
  output pj_c,
  output pj_z
);

  wire and_1_out, and_2_out, and_3_out, and_4_out, and_5_out, and_6_out, and_7_out, and_8_out, clock_1_out,
       d0, d1, d2, negq0, negq1, negq3, not_1_out, q0, q1, q3;

  Clock clock_1 (.out(clock_1_out));
  D_Flip_Flop d_ff_1 (.D(x), .clk(clock_1_out), .Q(q3), .Qn(negq3));  // open: preset, reset
  not not_1 (not_1_out, x);
  D_Flip_Flop d_ff_2 (.D(d2), .clk(clock_1_out), .Q(pj_z), .Qn(pj_c));  // open: preset, reset
  and and_1 (and_1_out, pj_z, negq1);
  and and_2 (and_2_out, pj_z, negq0);
  and and_3 (and_3_out, negq0, negq1);
  or or_1 (d2, and_1_out, and_2_out, and_3_out);
  and and_4 (and_4_out, pj_z, q0);
  and and_5 (and_5_out, pj_z, q1);
  and and_6 (and_6_out, negq0, negq3);
  and and_7 (and_7_out, pj_c, negq3, not_1_out);
  D_Flip_Flop d_ff_3 (.D(d1), .clk(clock_1_out), .Q(q1), .Qn(negq1));  // open: preset, reset
  or or_2 (d0, and_6_out, and_7_out);
  or or_3 (d1, and_4_out, and_5_out);
  D_Flip_Flop d_ff_4 (.D(d0), .clk(clock_1_out), .Q(q0), .Qn(negq0));  // open: preset, reset
  and and_8 (and_8_out, negq0, negq1);
  and and_9 (zuto, negq0, pj_c);
  and and_10 (zeleno, pj_c, negq1, negq3);
  or or_4 (crveno, and_8_out, pj_z);

  // Other names for the same wires on the sheet: negq2 = pj_c; q2 = pj_z
endmodule

module SEMAFOR (
);

  wire button_1_out, semafor_main_1_crveno, semafor_main_1_pj_c, semafor_main_1_pj_z, semafor_main_1_zeleno,
       semafor_main_1_zuto;

  Button button_1 (.out(button_1_out));
  Semafor_main semafor_main_1 (
    .x(button_1_out), .crveno(semafor_main_1_crveno), .zuto(semafor_main_1_zuto),
    .zeleno(semafor_main_1_zeleno), .pj_c(semafor_main_1_pj_c), .pj_z(semafor_main_1_pj_z));
  LED led_1 (.in(semafor_main_1_crveno));
  LED led_2 (.in(semafor_main_1_zuto));
  LED led_3 (.in(semafor_main_1_zeleno));
  LED led_4 (.in(semafor_main_1_pj_c));
  LED led_5 (.in(semafor_main_1_pj_z));
endmodule
