// Logisim project Zadatak_1.circ as structural Verilog: 2 circuits, main circuit T_FF
module T_FF (
  output [2:0] out_1
);

  wire and_1_out, and_2_out, and_3_out, and_4_out, and_5_out, and_6_out, clock_1_out, negQ0, negQ1, negQ2,
       Q0, Q1, Q2;

  Clock clock_1 (.out(clock_1_out));
  T_Flip_Flop T2 (.T(and_1_out), .clk(clock_1_out), .Q(Q2), .Qn(negQ2));  // open: reset, preset
  and and_1 (and_1_out, Q1, Q0);
  T_Flip_Flop T1 (.T(Q0), .clk(clock_1_out), .Q(Q1), .Qn(negQ1));  // open: reset, preset
  T_Flip_Flop T0 (.T(1'b1), .clk(clock_1_out), .Q(Q0), .Qn(negQ0));  // open: reset, preset
  and and_2 (and_2_out, negQ2, negQ1, Q0);
  and and_3 (and_3_out, Q2, Q1, Q0);
  and and_4 (and_4_out, Q2, negQ1, negQ0);
  and and_5 (and_5_out, negQ2, negQ1);
  and and_6 (and_6_out, Q2, Q1);
  or or_1 (out_1[2], Q0, Q1);
  or or_2 (out_1[1], and_2_out, and_3_out, and_4_out);
  or or_3 (out_1[0], and_5_out, and_6_out, negQ0);
  // Probe on out_1
endmodule

module JK_FF (
  output [2:0] out_1
);

  wire and_1_out, and_2_out, and_3_out, and_4_out, and_5_out, and_6_out, clock_1_out, negQ0, negQ1, negQ2,
       Q0, Q1, Q2;

  and and_1 (and_1_out, Q1, Q0);
  J_K_Flip_Flop JK2 (.J(and_1_out), .K(and_1_out), .clk(clock_1_out), .Q(Q2), .Qn(negQ2));  // open: preset, reset
  Clock clock_1 (.out(clock_1_out));
  J_K_Flip_Flop JK1 (.J(Q0), .K(Q0), .clk(clock_1_out), .Q(Q1), .Qn(negQ1));  // open: preset, reset
  J_K_Flip_Flop JK0 (.J(1'b1), .K(1'b1), .clk(clock_1_out), .Q(Q0), .Qn(negQ0));  // open: preset, reset
  and and_2 (and_2_out, negQ2, negQ1, Q0);
  and and_3 (and_3_out, Q2, Q1, Q0);
  and and_4 (and_4_out, negQ2, negQ1);
  and and_5 (and_5_out, Q2, Q1);
  and and_6 (and_6_out, Q2, negQ1, negQ0);
  or or_1 (out_1[2], Q0, Q1);
  or or_2 (out_1[1], and_2_out, and_3_out, and_6_out);
  or or_3 (out_1[0], and_4_out, and_5_out, negQ0);
  // Probe on out_1
endmodule
