// Logisim project Zadatak_2.circ as structural Verilog: 2 circuits, main circuit Moore
module Moore (
  input  in_1,
  output Y
);

  wire and_1_out, and_2_out, and_3_out, and_4_out, and_5_out, and_6_out, and_7_out, and_8_out, and_9_out,
       and_10_out, and_11_out, and_12_out, and_13_out, and_14_out, clock_1_out, negQ0, negQ1, negQ2, negQ3,
       not_1_out, not_2_out, not_3_out, not_4_out, not_5_out, not_6_out, Q0, Q1, Q2, Q3, T0, T1, T2, T3;

  not not_1 (not_1_out, in_1);
  not not_2 (not_2_out, in_1);
  not not_3 (not_3_out, in_1);
  not not_4 (not_4_out, in_1);
  not not_5 (not_5_out, in_1);
  not not_6 (not_6_out, in_1);
  and and_1 (and_1_out, in_1, Q1, Q2, negQ0);
  and and_2 (and_2_out, Q1, not_1_out);
  and and_3 (and_3_out, Q2, Q1);
  and and_4 (and_4_out, Q2, not_2_out, negQ0);
  and and_5 (and_5_out, in_1, Q2, Q0);
  and and_6 (and_6_out, not_3_out, Q0);
  and and_7 (and_7_out, Q1, Q0);
  and and_8 (and_8_out, in_1, Q2);
  and and_9 (and_9_out, not_4_out, Q1, negQ2);
  and and_10 (and_10_out, negQ0, negQ2, in_1);
  and and_11 (and_11_out, Q2, Q1, not_5_out, Q0);
  and and_12 (and_12_out, negQ2, negQ1, not_6_out, Q0);
  or or_1 (T3, Q3, and_1_out);
  or or_2 (T2, and_2_out, and_3_out, and_4_out, and_5_out);
  or or_3 (T1, and_6_out, and_7_out, and_8_out, and_9_out);
  or or_4 (T0, and_10_out, and_11_out, and_12_out);
  Clock clock_1 (.out(clock_1_out));
  T_Flip_Flop u_T3 (.T(T3), .clk(clock_1_out), .Q(Q3), .Qn(negQ3));  // open: reset, preset
  T_Flip_Flop u_T2 (.T(T2), .clk(clock_1_out), .Q(Q2), .Qn(negQ2));  // open: reset, preset
  T_Flip_Flop u_T1 (.T(T1), .clk(clock_1_out), .Q(Q1), .Qn(negQ1));  // open: reset, preset
  and and_13 (and_13_out, Q0, Q1, Q2, negQ3);
  and and_14 (and_14_out, negQ0, negQ1, negQ2, Q3);
  or or_5 (Y, and_13_out, and_14_out);
  T_Flip_Flop u_T0 (.T(T0), .clk(clock_1_out), .Q(Q0), .Qn(negQ0));  // open: reset, preset
endmodule

module Mealy (
  input  in_1,
  output Y
);

  wire and_1_out, and_2_out, and_3_out, and_4_out, and_5_out, and_6_out, and_7_out, and_8_out, and_9_out,
       and_10_out, and_11_out, and_12_out, clock_1_out, not_1_out, not_2_out, not_3_out, not_4_out, Q0,
       Q0neg, Q1, Q1neg, Q2, Q2neg, T0, T1, T2;

  Clock clock_1 (.out(clock_1_out));
  not not_1 (not_1_out, in_1);
  not not_2 (not_2_out, in_1);
  T_Flip_Flop u_T2 (.T(T2), .clk(clock_1_out), .Q(Q2), .Qn(Q2neg));  // open: reset, preset
  and and_1 (and_1_out, Q2, not_1_out);
  and and_2 (and_2_out, Q2, Q0);
  and and_3 (and_3_out, Q2, Q1);
  not not_3 (not_3_out, in_1);
  and and_4 (and_4_out, Q1, not_1_out);
  and and_5 (and_5_out, Q0, Q1);
  and and_6 (and_6_out, Q2, in_1);
  and and_7 (and_7_out, Q0, not_2_out, Q2neg);
  and and_8 (and_8_out, Q2neg, Q1, not_2_out);
  and and_9 (and_9_out, Q0neg, Q2neg, in_1);
  and and_10 (and_10_out, not_3_out, Q1neg, Q0);
  T_Flip_Flop u_T1 (.T(T1), .clk(clock_1_out), .Q(Q1), .Qn(Q1neg));  // open: reset, preset
  or or_1 (T2, and_4_out, and_1_out, and_2_out, and_3_out);
  or or_2 (T1, and_5_out, and_6_out, and_7_out, and_8_out);
  or or_3 (T0, and_9_out, and_10_out);
  T_Flip_Flop u_T0 (.T(T0), .clk(clock_1_out), .Q(Q0), .Qn(Q0neg));  // open: reset, preset
  not not_4 (not_4_out, in_1);
  and and_11 (and_11_out, Q2, Q0, Q1neg, not_4_out);
  and and_12 (and_12_out, in_1, Q2, Q1, Q0neg);
  or or_4 (Y, and_11_out, and_12_out);
endmodule
