// Logisim project Zadatak_3.circ as structural Verilog: 5 circuits, main circuit main
module main (
  input  cin,
  output [3:0] out_2,
  output [3:0] out_3,
  output [3:0] out_4,
  output [3:0] out_5,
  output [3:0] out_6,
  output [3:0] out_7,
  output [3:0] out_8,
  output [3:0] out_9
);

  wire brojac_cifri_1_out_2, clock_1_out, poredjivac_1_out_3, poredjivac_2_out_3, poredjivac_3_out_3,
       poredjivac_4_out_3, poredjivac_5_out_3, poredjivac_6_out_3, poredjivac_7_out_3, poredjivac_8_out_3;
  wire [2:0] d_ff_1_q, xnor_1_out, xnor_2_out, xnor_3_out, xnor_4_out, xnor_5_out, xnor_6_out, xnor_7_out,
       xnor_8_out;

  D_Flip_Flop d_ff_1 (.D(cin), .clk(clock_1_out), .Q(d_ff_1_q[0]));  // open: Qn, preset, reset
  Clock clock_1 (.out(clock_1_out));
  D_Flip_Flop d_ff_2 (.D(d_ff_1_q[0]), .clk(clock_1_out), .Q(d_ff_1_q[1]));  // open: Qn, preset, reset
  // Probe on brojac_cifri_1_out_2
  brojac_cifri brojac_cifri_1 (.clock(clock_1_out), .out_2(brojac_cifri_1_out_2));
  D_Flip_Flop d_ff_3 (.D(d_ff_1_q[1]), .clk(clock_1_out), .Q(d_ff_1_q[2]));  // open: Qn, preset, reset
  // Probe on d_ff_1_q
  assign xnor_1_out = ~(d_ff_1_q ^ 3'b000);  // XNOR_Gate xnor_1, 3 bits wide
  assign xnor_2_out = ~(d_ff_1_q ^ 3'b001);  // XNOR_Gate xnor_2, 3 bits wide
  assign xnor_3_out = ~(d_ff_1_q ^ 3'b010);  // XNOR_Gate xnor_3, 3 bits wide
  assign xnor_4_out = ~(d_ff_1_q ^ 3'b011);  // XNOR_Gate xnor_4, 3 bits wide
  assign xnor_5_out = ~(d_ff_1_q ^ 3'b100);  // XNOR_Gate xnor_5, 3 bits wide
  assign xnor_6_out = ~(d_ff_1_q ^ 3'b101);  // XNOR_Gate xnor_6, 3 bits wide
  assign xnor_7_out = ~(d_ff_1_q ^ 3'b110);  // XNOR_Gate xnor_7, 3 bits wide
  assign xnor_8_out = ~(d_ff_1_q ^ 3'b111);  // XNOR_Gate xnor_8, 3 bits wide
  poredjivac poredjivac_1 (.x(xnor_1_out), .br(brojac_cifri_1_out_2), .out_3(poredjivac_1_out_3));
  poredjivac poredjivac_2 (.x(xnor_2_out), .br(brojac_cifri_1_out_2), .out_3(poredjivac_2_out_3));
  poredjivac poredjivac_3 (.x(xnor_3_out), .br(brojac_cifri_1_out_2), .out_3(poredjivac_3_out_3));
  poredjivac poredjivac_4 (.x(xnor_4_out), .br(brojac_cifri_1_out_2), .out_3(poredjivac_4_out_3));
  poredjivac poredjivac_5 (.x(xnor_5_out), .br(brojac_cifri_1_out_2), .out_3(poredjivac_5_out_3));
  poredjivac poredjivac_6 (.x(xnor_6_out), .br(brojac_cifri_1_out_2), .out_3(poredjivac_6_out_3));
  poredjivac poredjivac_7 (.x(xnor_7_out), .br(brojac_cifri_1_out_2), .out_3(poredjivac_7_out_3));
  poredjivac poredjivac_8 (.x(xnor_8_out), .br(brojac_cifri_1_out_2), .out_3(poredjivac_8_out_3));
  // Probe on poredjivac_1_out_3
  // Probe on poredjivac_2_out_3
  // Probe on poredjivac_3_out_3
  // Probe on poredjivac_4_out_3
  // Probe on poredjivac_5_out_3
  // Probe on poredjivac_6_out_3
  // Probe on poredjivac_7_out_3
  // Probe on poredjivac_8_out_3
  brojac_mod10 brojac_mod10_1 (.clock(poredjivac_1_out_3), .out_2(out_2));
  brojac_mod10 brojac_mod10_2 (.clock(poredjivac_2_out_3), .out_2(out_3));
  brojac_mod10 brojac_mod10_3 (.clock(poredjivac_3_out_3), .out_2(out_4));
  brojac_mod10 brojac_mod10_4 (.clock(poredjivac_4_out_3), .out_2(out_5));
  brojac_mod10 brojac_mod10_5 (.clock(poredjivac_5_out_3), .out_2(out_6));
  brojac_mod10 brojac_mod10_6 (.clock(poredjivac_6_out_3), .out_2(out_7));
  brojac_mod10 brojac_mod10_7 (.clock(poredjivac_7_out_3), .out_2(out_8));
  brojac_mod10 brojac_mod10_8 (.clock(poredjivac_8_out_3), .out_2(out_9));
  // Probe on out_2
  // Probe on out_3
  // Probe on out_4
  // Probe on out_5
  // Probe on out_6
  // Probe on out_7
  // Probe on out_8
  // Probe on out_9
endmodule

module brojac_cifri (
  input  clock,
  output out_2
);

  wire or_1_out, T0_q, T1_q;

  T_Flip_Flop T1 (.T(T0_q), .clk(clock), .Q(T1_q));  // open: Qn, reset, preset
  T_Flip_Flop T0 (.T(or_1_out), .clk(clock), .Q(T0_q));  // open: Qn, reset, preset
  or or_1 (or_1_out, ~T1_q, ~T0_q);  // OR_Gate
  and and_1 (out_2, T0_q, T1_q);
endmodule

module brojac_mod10 (
  input  clock,
  output [3:0] out_2
);

  wire and_1_out, and_2_out, and_3_out, and_4_out, negQ0, negQ1, negQ2, negQ3, or_1_out;

  and and_1 (and_1_out, out_2[3], out_2[0]);
  and and_2 (and_2_out, out_2[2], out_2[1], out_2[0]);
  T_Flip_Flop T3 (.T(or_1_out), .clk(clock), .Q(out_2[3]), .Qn(negQ3));  // open: reset, preset
  or or_1 (or_1_out, and_1_out, and_2_out);
  // Probe on out_2
  T_Flip_Flop T2 (.T(and_3_out), .clk(clock), .Q(out_2[2]), .Qn(negQ2));  // open: reset, preset
  and and_3 (and_3_out, out_2[1], out_2[0]);
  and and_4 (and_4_out, ~out_2[3], out_2[0]);  // AND_Gate
  T_Flip_Flop T1 (.T(and_4_out), .clk(clock), .Q(out_2[1]), .Qn(negQ1));  // open: reset, preset
  T_Flip_Flop T0 (.T(1'b1), .clk(clock), .Q(out_2[0]), .Qn(negQ0));  // open: reset, preset

  // Other names for the same wires on the sheet: Q0 = out_2[0]; Q1 = out_2[1]; Q2 = out_2[2]; Q3 = out_2[3]
endmodule

module D_FF (
  input  x,
  input  clock,
  output [2:0] out_3
);

  D_Flip_Flop d_ff_1 (.D(x), .clk(clock), .Q(out_3[0]));  // open: Qn, preset, reset
  D_Flip_Flop d_ff_2 (.D(out_3[0]), .clk(clock), .Q(out_3[1]));  // open: Qn, preset, reset
  D_Flip_Flop d_ff_3 (.D(out_3[1]), .clk(clock), .Q(out_3[2]));  // open: Qn, preset, reset
endmodule

module poredjivac (
  input  [2:0] x,
  input  br,
  output out_3
);

  wire and_1_out, xnor_1_out, xnor_2_out, xnor_3_out;

  // Probe on x
  xnor xnor_1 (xnor_1_out, 1'b1, x[0]);
  xnor xnor_2 (xnor_2_out, 1'b1, x[1]);
  xnor xnor_3 (xnor_3_out, 1'b1, x[2]);
  // Probe on and_1_out
  and and_1 (and_1_out, xnor_1_out, xnor_2_out, xnor_3_out);
  and and_2 (out_3, and_1_out, br);
endmodule
